// Logisim project Binary_To_BCD.circ as structural Verilog
module Binary_To_BCD (
  input  B0,
  input  B1,
  input  B2,
  input  B3,
  input  B4,
  input  B5,
  input  B6,
  input  B7,
  output out_9,
  output out_10,
  output out_11,
  output out_12,
  output out_13,
  output out_14,
  output out_15,
  output out_16,
  output out_17,
  output out_18,
  output out_19,
  output out_20
);

  wire c_1_s0, c_1_s1, c_1_s2, c_1_s3, c_2_s0, c_2_s1, c_2_s2, c_2_s3, c_3_s0, c_3_s1, c_3_s2, c_3_s3,
       c_4_s0, c_4_s1, c_4_s2, c_4_s3, c_5_s0, c_5_s1, c_5_s2;

  C c_1 (.A(B5), .B(B6), .C(B7), .D(1'b0), .S0(c_1_s0), .S1(c_1_s1), .S2(c_1_s2), .S3(c_1_s3));
  C c_2 (.A(B4), .B(c_1_s0), .C(c_1_s1), .D(c_1_s2), .S0(c_2_s0), .S1(c_2_s1), .S2(c_2_s2), .S3(c_2_s3));
  C c_3 (.A(B3), .B(c_2_s0), .C(c_2_s1), .D(c_2_s2), .S0(c_3_s0), .S1(c_3_s1), .S2(c_3_s2), .S3(c_3_s3));
  C c_4 (.A(B2), .B(c_3_s0), .C(c_3_s1), .D(c_3_s2), .S0(c_4_s0), .S1(c_4_s1), .S2(c_4_s2), .S3(c_4_s3));
  C c_5 (.A(c_3_s3), .B(c_2_s3), .C(c_1_s3), .D(1'b0), .S0(c_5_s0), .S1(c_5_s1), .S2(c_5_s2), .S3(out_18));
  C c_6 (.A(B1), .B(c_4_s0), .C(c_4_s1), .D(c_4_s2), .S0(out_10), .S1(out_11), .S2(out_12), .S3(out_13));
  C c_7 (.A(c_4_s3), .B(c_5_s0), .C(c_5_s1), .D(c_5_s2), .S0(out_14), .S1(out_15), .S2(out_16), .S3(out_17));

  assign out_9 = B0;
  assign out_19 = 1'b0;
  assign out_20 = 1'b0;

  // Notes on the sheet:
  //   C1
  //   C2
  //   C3
  //   C4
  //   C6
  //   C5
  //   C7
endmodule

module C (
  input  A,
  input  B,
  input  C,
  input  D,
  output S0,
  output S1,
  output S2,
  output S3
);

  wire and_1_out, and_2_out, and_3_out, and_4_out, and_5_out, and_6_out, and_7_out, and_8_out, and_9_out,
       and_10_out, and_11_out, and_12_out, and_13_out, not_1_out, not_2_out, not_3_out, not_4_out, or_1_out,
       or_2_out, or_4_out;

  not not_1 (not_1_out, A);
  not not_2 (not_2_out, B);
  not not_3 (not_3_out, C);
  not not_4 (not_4_out, D);
  and and_1 (and_1_out, not_1_out, D);
  and and_2 (and_2_out, not_4_out, not_3_out);
  and and_3 (and_3_out, and_2_out, A);
  and and_4 (and_4_out, C, B);
  and and_5 (and_5_out, and_4_out, not_1_out);
  and and_6 (and_6_out, not_3_out, B);
  and and_7 (and_7_out, B, A);
  and and_8 (and_8_out, D, not_1_out);
  and and_9 (and_9_out, D, A);
  and and_10 (and_10_out, not_1_out, not_2_out);
  and and_11 (and_11_out, and_10_out, C);
  or or_1 (or_1_out, and_1_out, and_3_out);
  or or_2 (or_2_out, and_6_out, and_7_out);
  or or_3 (S2, and_9_out, and_11_out);
  or or_4 (or_4_out, D, and_12_out);
  and and_12 (and_12_out, C, A);
  and and_13 (and_13_out, B, C);
  or or_5 (S0, or_1_out, and_5_out);
  or or_6 (S1, or_2_out, and_8_out);
  or or_7 (S3, or_4_out, and_13_out);
endmodule
