// Logisim project Divider.circ as structural Verilog: 3 circuits, main circuit main
module main (
  input  A0,
  input  A1,
  input  A2,
  input  A3,
  input  A4,
  input  B0,
  input  B1,
  input  B2,
  input  B3,
  input  B4,
  output out_11,
  output out_12,
  output out_13,
  output out_14,
  output out_15,
  output out_16
);

  Dividor dividor_1 (
    .A0(A0), .A1(A1), .A2(A2), .A3(A3), .A4(A4), .B0(B0), .B1(B1), .B2(B2), .B3(B3), .B4(B4), .Q0(out_11),
    .Q1(out_12), .Q2(out_13), .Q3(out_14), .Q4(out_15), .Dev_0_Flag(out_16));
endmodule

module Dividor (
  input  A0,
  input  A1,
  input  A2,
  input  A3,
  input  A4,
  input  B0,
  input  B1,
  input  B2,
  input  B3,
  input  B4,
  output Q0,
  output Q1,
  output Q2,
  output Q3,
  output Q4,
  output Dev_0_Flag
);

  wire full_subtractor_1_borrow_out, full_subtractor_1_difference, full_subtractor_2_borrow_out,
       full_subtractor_2_difference, full_subtractor_3_borrow_out, full_subtractor_3_difference,
       full_subtractor_4_borrow_out, full_subtractor_4_difference, full_subtractor_5_borrow_out,
       full_subtractor_5_difference, full_subtractor_6_borrow_out, full_subtractor_6_difference,
       full_subtractor_7_borrow_out, full_subtractor_7_difference, full_subtractor_8_borrow_out,
       full_subtractor_8_difference, full_subtractor_9_borrow_out, full_subtractor_9_difference,
       full_subtractor_10_borrow_out, full_subtractor_10_difference, full_subtractor_11_borrow_out,
       full_subtractor_11_difference, full_subtractor_12_borrow_out, full_subtractor_12_difference,
       full_subtractor_13_borrow_out, full_subtractor_14_borrow_out, full_subtractor_15_borrow_out,
       full_subtractor_16_borrow_out, full_subtractor_16_difference, multiplexer_1_out, multiplexer_2_out,
       multiplexer_3_out, multiplexer_4_out, multiplexer_5_out, multiplexer_6_out, multiplexer_7_out,
       multiplexer_8_out, multiplexer_9_out, or_1_out, or_2_out;

  Full_Subtractor full_subtractor_1 (
    .A(A3), .B(B0), .Borrow_In(1'b0), .Difference(full_subtractor_1_difference),
    .Borrow_Out(full_subtractor_1_borrow_out));
  Full_Subtractor full_subtractor_2 (
    .A(1'b0), .B(B1), .Borrow_In(full_subtractor_1_borrow_out), .Difference(full_subtractor_2_difference),
    .Borrow_Out(full_subtractor_2_borrow_out));
  Full_Subtractor full_subtractor_3 (
    .A(1'b0), .B(B2), .Borrow_In(full_subtractor_2_borrow_out), .Difference(full_subtractor_3_difference),
    .Borrow_Out(full_subtractor_3_borrow_out));
  Full_Subtractor full_subtractor_4 (
    .A(1'b0), .B(B3), .Borrow_In(full_subtractor_3_borrow_out), .Difference(full_subtractor_4_difference),
    .Borrow_Out(full_subtractor_4_borrow_out));
  Multiplexer #(.enable("false")) multiplexer_1 (
    .in0(full_subtractor_1_difference), .in1(A3), .out(multiplexer_1_out), .sel(full_subtractor_4_borrow_out));
  Multiplexer #(.enable("false")) multiplexer_2 (
    .in0(full_subtractor_2_difference), .in1(1'b0), .out(multiplexer_2_out),
    .sel(full_subtractor_4_borrow_out));
  Multiplexer #(.enable("false")) multiplexer_3 (
    .in0(full_subtractor_3_difference), .in1(1'b0), .out(multiplexer_3_out),
    .sel(full_subtractor_4_borrow_out));
  Full_Subtractor full_subtractor_5 (
    .A(A2), .B(B0), .Borrow_In(1'b0), .Difference(full_subtractor_5_difference),
    .Borrow_Out(full_subtractor_5_borrow_out));
  Full_Subtractor full_subtractor_6 (
    .A(multiplexer_1_out), .B(B1), .Borrow_In(full_subtractor_5_borrow_out),
    .Difference(full_subtractor_6_difference), .Borrow_Out(full_subtractor_6_borrow_out));
  Full_Subtractor full_subtractor_7 (
    .A(multiplexer_2_out), .B(B2), .Borrow_In(full_subtractor_6_borrow_out),
    .Difference(full_subtractor_7_difference), .Borrow_Out(full_subtractor_7_borrow_out));
  Full_Subtractor full_subtractor_8 (
    .A(multiplexer_3_out), .B(B3), .Borrow_In(full_subtractor_7_borrow_out),
    .Difference(full_subtractor_8_difference), .Borrow_Out(full_subtractor_8_borrow_out));
  Multiplexer #(.enable("false")) multiplexer_4 (
    .in0(full_subtractor_5_difference), .in1(A2), .out(multiplexer_4_out), .sel(full_subtractor_8_borrow_out));
  Multiplexer #(.enable("false")) multiplexer_5 (
    .in0(full_subtractor_6_difference), .in1(multiplexer_1_out), .out(multiplexer_5_out),
    .sel(full_subtractor_8_borrow_out));
  Multiplexer #(.enable("false")) multiplexer_6 (
    .in0(full_subtractor_7_difference), .in1(multiplexer_2_out), .out(multiplexer_6_out),
    .sel(full_subtractor_8_borrow_out));
  Full_Subtractor full_subtractor_9 (
    .A(A1), .B(B0), .Borrow_In(1'b0), .Difference(full_subtractor_9_difference),
    .Borrow_Out(full_subtractor_9_borrow_out));
  Full_Subtractor full_subtractor_10 (
    .A(multiplexer_4_out), .B(B1), .Borrow_In(full_subtractor_9_borrow_out),
    .Difference(full_subtractor_10_difference), .Borrow_Out(full_subtractor_10_borrow_out));
  Full_Subtractor full_subtractor_11 (
    .A(multiplexer_5_out), .B(B2), .Borrow_In(full_subtractor_10_borrow_out),
    .Difference(full_subtractor_11_difference), .Borrow_Out(full_subtractor_11_borrow_out));
  Full_Subtractor full_subtractor_12 (
    .A(multiplexer_6_out), .B(B3), .Borrow_In(full_subtractor_11_borrow_out),
    .Difference(full_subtractor_12_difference), .Borrow_Out(full_subtractor_12_borrow_out));
  Multiplexer #(.enable("false")) multiplexer_7 (
    .in0(full_subtractor_9_difference), .in1(A1), .out(multiplexer_7_out), .sel(full_subtractor_12_borrow_out));
  Multiplexer #(.enable("false")) multiplexer_8 (
    .in0(full_subtractor_10_difference), .in1(multiplexer_4_out), .out(multiplexer_8_out),
    .sel(full_subtractor_12_borrow_out));
  Multiplexer #(.enable("false")) multiplexer_9 (
    .in0(full_subtractor_11_difference), .in1(multiplexer_5_out), .out(multiplexer_9_out),
    .sel(full_subtractor_12_borrow_out));
  Full_Subtractor full_subtractor_13 (
    .A(A0), .B(B0), .Borrow_In(1'b0), .Borrow_Out(full_subtractor_13_borrow_out));  // open: Difference
  Full_Subtractor full_subtractor_14 (
    .A(multiplexer_7_out), .B(B1), .Borrow_In(full_subtractor_13_borrow_out),
    .Borrow_Out(full_subtractor_14_borrow_out));  // open: Difference
  Full_Subtractor full_subtractor_15 (
    .A(multiplexer_8_out), .B(B2), .Borrow_In(full_subtractor_14_borrow_out),
    .Borrow_Out(full_subtractor_15_borrow_out));  // open: Difference
  Full_Subtractor full_subtractor_16 (
    .A(multiplexer_9_out), .B(B3), .Borrow_In(full_subtractor_15_borrow_out),
    .Difference(full_subtractor_16_difference), .Borrow_Out(full_subtractor_16_borrow_out));
  not not_1 (Q0, full_subtractor_16_borrow_out);
  not not_2 (Q1, full_subtractor_12_borrow_out);
  not not_3 (Q2, full_subtractor_8_borrow_out);
  not not_4 (Q3, full_subtractor_4_borrow_out);
  xor xor_1 (Q4, A4, B4);
  or or_1 (or_1_out, B2, B3);
  or or_2 (or_2_out, or_1_out, B1);
  nor nor_1 (Dev_0_Flag, or_2_out, B0);
endmodule

module Full_Subtractor (
  input  A,
  input  B,
  input  Borrow_In,
  output Difference,
  output Borrow_Out
);

  wire and_1_out, and_2_out, and_3_out, not_1_out, or_1_out, xor_1_out;

  not not_1 (not_1_out, A);
  and and_1 (and_1_out, not_1_out, B);
  and and_2 (and_2_out, not_1_out, Borrow_In);
  and and_3 (and_3_out, B, Borrow_In);
  xor xor_1 (xor_1_out, A, B);
  xor xor_2 (Difference, xor_1_out, Borrow_In);
  or or_1 (or_1_out, and_1_out, and_2_out);
  or or_2 (Borrow_Out, or_1_out, and_3_out);
endmodule
