// Logisim project Final Subtraction and addition.circ as structural Verilog
module Adder_and_subtracter (
  input  [3:0] B,
  input  [3:0] A,
  input  A_sign,
  input  B_sign,
  input  Cin,
  output Sign,
  output Cout,
  output Out_3,
  output Out_2,
  output Out_1,
  output Out_0
);

  wire and_1_out, and_3_out, and_4_out, and_5_out, full_adder_me_1_cin_2, full_adder_me_1_sum,
       full_adder_me_2_cin_2, full_adder_me_2_sum, full_adder_me_3_cin_2, full_adder_me_3_sum,
       full_adder_me_4_cin_2, full_adder_me_4_sum, not_1_out, not_2_out, not_3_out, not_4_out, or_2_out,
       twos_complement_1_outa, twos_complement_1_outb, twos_complement_1_outc, twos_complement_1_outd,
       xor_1_out, xor_2_out, xor_3_out, xor_4_out, xor_5_out, xor_6_out, xor_7_out, xor_8_out, xor_9_out,
       xor_10_out;

  xor xor_1 (xor_1_out, B[3], and_3_out);
  not not_1 (not_1_out, full_adder_me_1_cin_2);
  and and_1 (and_1_out, not_1_out, xor_10_out);
  or or_1 (Sign, and_5_out, and_1_out);
  xor xor_2 (xor_2_out, A[3], and_4_out);
  Full_Adder_ME full_adder_me_1 (
    .Input_2(xor_1_out), .Inout_1(xor_2_out), .Cin(full_adder_me_2_cin_2), .Cin_2(full_adder_me_1_cin_2),
    .Sum(full_adder_me_1_sum));
  not not_2 (not_2_out, xor_10_out);
  and and_2 (Cout, full_adder_me_1_cin_2, not_2_out);
  xor xor_3 (xor_3_out, B[2], and_3_out);
  Multiplexer #(.enable("false")) multiplexer_1 (
    .in0(full_adder_me_1_sum), .in1(twos_complement_1_outa), .out(Out_3), .sel(and_1_out));
  xor xor_4 (xor_4_out, A[2], and_4_out);
  Full_Adder_ME full_adder_me_2 (
    .Input_2(xor_3_out), .Inout_1(xor_4_out), .Cin(full_adder_me_3_cin_2), .Cin_2(full_adder_me_2_cin_2),
    .Sum(full_adder_me_2_sum));
  xor xor_5 (xor_5_out, B[1], and_3_out);
  xor xor_6 (xor_6_out, A[1], and_4_out);
  Full_Adder_ME full_adder_me_3 (
    .Input_2(xor_5_out), .Inout_1(xor_6_out), .Cin(full_adder_me_4_cin_2), .Cin_2(full_adder_me_3_cin_2),
    .Sum(full_adder_me_3_sum));
  Multiplexer #(.enable("false")) multiplexer_2 (
    .in0(full_adder_me_2_sum), .in1(twos_complement_1_outb), .out(Out_2), .sel(and_1_out));
  xor xor_7 (xor_7_out, B[0], and_3_out);
  xor xor_8 (xor_8_out, A[0], and_4_out);
  Full_Adder_ME full_adder_me_4 (
    .Input_2(xor_7_out), .Inout_1(xor_8_out), .Cin(or_2_out), .Cin_2(full_adder_me_4_cin_2),
    .Sum(full_adder_me_4_sum));
  Twos_complement twos_complement_1 (
    .a(full_adder_me_1_sum), .b(full_adder_me_2_sum), .c(full_adder_me_3_sum), .d(full_adder_me_4_sum),
    .outa(twos_complement_1_outa), .outb(twos_complement_1_outb), .outc(twos_complement_1_outc),
    .outd(twos_complement_1_outd));
  and and_3 (and_3_out, not_3_out, xor_9_out);
  and and_4 (and_4_out, not_4_out, A_sign);
  or or_2 (or_2_out, and_3_out, and_4_out);
  Multiplexer #(.enable("false")) multiplexer_3 (
    .in0(full_adder_me_3_sum), .in1(twos_complement_1_outc), .out(Out_1), .sel(and_1_out));
  not not_3 (not_3_out, A_sign);
  not not_4 (not_4_out, xor_9_out);
  xor xor_9 (xor_9_out, B_sign, Cin);
  xor xor_10 (xor_10_out, A_sign, xor_9_out);
  Multiplexer #(.enable("false")) multiplexer_4 (
    .in0(twos_complement_1_outd), .in1(full_adder_me_4_sum), .out(Out_0), .sel(and_1_out));
  and and_5 (and_5_out, A_sign, xor_9_out);

  // Notes on the sheet:
  //   Two opposite
  //   Cout
endmodule

module Twos_complement (
  input  a,
  input  b,
  input  c,
  input  d,
  output outa,
  output outb,
  output outc,
  output outd
);

  wire or_1_out, or_2_out;

  xor xor_1 (outa, or_1_out, a);
  or or_1 (or_1_out, b, or_2_out);
  xor xor_2 (outb, or_2_out, b);
  or or_2 (or_2_out, c, d);
  xor xor_3 (outc, d, c);

  assign outd = d;
endmodule

module Full_Adder_ME (
  input  Input_2,
  input  Inout_1,
  input  Cin,
  output Cin_2,
  output Sum
);

  wire and_1_out, and_2_out, xor_1_out;

  and and_1 (and_1_out, Input_2, Inout_1);
  or or_1 (Cin_2, and_1_out, and_2_out);
  xor xor_1 (xor_1_out, Input_2, Inout_1);
  xor xor_2 (Sum, xor_1_out, Cin);
  and and_2 (and_2_out, xor_1_out, Cin);
endmodule
