// Logisim project Final circuit .circ as structural Verilog: 2 circuits, main circuit main
module main (
  input  in_1,
  input  in_2,
  input  [4:0] A,
  input  [4:0] B
);

  wire final_circuit_1__7_segment_1_a, final_circuit_1__7_segment_1_c, final_circuit_1__7_segment_1_d,
       final_circuit_1__7_segment_1_e, final_circuit_1__7_segment_1_f, final_circuit_1__7_segment_1_g,
       final_circuit_1__7_segment_2_a, final_circuit_1__7_segment_2_b, final_circuit_1__7_segment_2_c,
       final_circuit_1__7_segment_2_d, final_circuit_1__7_segment_2_e, final_circuit_1__7_segment_2_f,
       final_circuit_1__7_segment_2_g, final_circuit_1__7_segment_3_a, final_circuit_1__7_segment_3_b,
       final_circuit_1__7_segment_3_c, final_circuit_1__7_segment_3_d, final_circuit_1__7_segment_3_e,
       final_circuit_1__7_segment_3_f, final_circuit_1__7_segment_3_g, final_circuit_1__7_segment__1_b,
       final_circuit_1_division_by_0, final_circuit_1_sign, final_circuit_1_zero_flag;

  Final_Circuit final_circuit_1 (
    .B(B), .A(A), .Zero_flag(final_circuit_1_zero_flag), .S2(in_1), .S1(in_2),
    .Division_by_0(final_circuit_1_division_by_0), .Sign(final_circuit_1_sign),
    ._7_Segment_1_a(final_circuit_1__7_segment_1_a), ._7_Segment__1_b(final_circuit_1__7_segment__1_b),
    ._7_Segment_1_c(final_circuit_1__7_segment_1_c), ._7_Segment_1_d(final_circuit_1__7_segment_1_d),
    ._7_Segment_1_e(final_circuit_1__7_segment_1_e), ._7_Segment_1_f(final_circuit_1__7_segment_1_f),
    ._7_Segment_1_g(final_circuit_1__7_segment_1_g), ._7_Segment_2_a(final_circuit_1__7_segment_2_a),
    ._7_Segment_2_b(final_circuit_1__7_segment_2_b), ._7_Segment_2_c(final_circuit_1__7_segment_2_c),
    ._7_Segment_2_d(final_circuit_1__7_segment_2_d), ._7_Segment_2_e(final_circuit_1__7_segment_2_e),
    ._7_Segment_2_f(final_circuit_1__7_segment_2_f), ._7_Segment_2_g(final_circuit_1__7_segment_2_g),
    ._7_Segment_3_a(final_circuit_1__7_segment_3_a), ._7_Segment_3_b(final_circuit_1__7_segment_3_b),
    ._7_Segment_3_c(final_circuit_1__7_segment_3_c), ._7_Segment_3_d(final_circuit_1__7_segment_3_d),
    ._7_Segment_3_e(final_circuit_1__7_segment_3_e), ._7_Segment_3_f(final_circuit_1__7_segment_3_f),
    ._7_Segment_3_g(final_circuit_1__7_segment_3_g));
  LED Division_By_0 (.in(final_circuit_1_division_by_0));
  LED Sign (.in(final_circuit_1_sign));
  LED _0_Flag (.in(final_circuit_1_zero_flag));
  _7_Segment_Display u_7_segment_display_1 (
    .g(final_circuit_1__7_segment_3_g), .f(final_circuit_1__7_segment_3_f),
    .a(final_circuit_1__7_segment_3_a), .b(final_circuit_1__7_segment_3_b),
    .e(final_circuit_1__7_segment_3_e), .d(final_circuit_1__7_segment_3_d), .c(final_circuit_1__7_segment_3_c));  // open: dp
  _7_Segment_Display u_7_segment_display_2 (
    .g(final_circuit_1__7_segment_2_g), .f(final_circuit_1__7_segment_2_f),
    .a(final_circuit_1__7_segment_2_a), .b(final_circuit_1__7_segment_2_b),
    .e(final_circuit_1__7_segment_2_e), .d(final_circuit_1__7_segment_2_d), .c(final_circuit_1__7_segment_2_c));  // open: dp
  _7_Segment_Display u_7_segment_display_3 (
    .g(final_circuit_1__7_segment_1_g), .f(final_circuit_1__7_segment_1_f),
    .a(final_circuit_1__7_segment_1_a), .b(final_circuit_1__7_segment__1_b),
    .e(final_circuit_1__7_segment_1_e), .d(final_circuit_1__7_segment_1_d), .c(final_circuit_1__7_segment_1_c));  // open: dp
endmodule

module Final_Circuit (
  input  [4:0] B,
  input  [4:0] A,
  input  S2,
  input  S1,
  output Division_by_0,
  output Sign,
  output Zero_flag,
  output _7_Segment_1_a,
  output _7_Segment__1_b,
  output _7_Segment_1_c,
  output _7_Segment_1_d,
  output _7_Segment_1_e,
  output _7_Segment_1_f,
  output _7_Segment_1_g,
  output _7_Segment_2_a,
  output _7_Segment_2_b,
  output _7_Segment_2_c,
  output _7_Segment_2_d,
  output _7_Segment_2_e,
  output _7_Segment_2_f,
  output _7_Segment_2_g,
  output _7_Segment_3_a,
  output _7_Segment_3_b,
  output _7_Segment_3_c,
  output _7_Segment_3_d,
  output _7_Segment_3_e,
  output _7_Segment_3_f,
  output _7_Segment_3_g
);

  wire adder_and_subtracter_1_cout, adder_and_subtracter_1_out_0, adder_and_subtracter_1_out_1,
       adder_and_subtracter_1_out_2, adder_and_subtracter_1_out_3, adder_and_subtracter_1_sign,
       binary_to_bcd_1_out_9, binary_to_bcd_1_out_10, binary_to_bcd_1_out_11, binary_to_bcd_1_out_12,
       binary_to_bcd_1_out_13, binary_to_bcd_1_out_14, binary_to_bcd_1_out_15, binary_to_bcd_1_out_16,
       binary_to_bcd_1_out_17, binary_to_bcd_1_out_18, binary_to_bcd_1_out_19, binary_to_bcd_1_out_20,
       dividor_1_q0, dividor_1_q1, dividor_1_q2, dividor_1_q3, dividor_1_q4, multiplication_1_z0,
       multiplication_1_z1, multiplication_1_z2, multiplication_1_z3, multiplication_1_z4,
       multiplication_1_z5, multiplication_1_z6, multiplication_1_z7, multiplication_1_z8, or_1_out,
       or_2_out, or_3_out, or_4_out, or_5_out, or_6_out, or_7_out;
  wire [7:0] multiplexer_9_out;

  Multiplexer #(.select(2), .enable("false")) multiplexer_1 (
    .in0(adder_and_subtracter_1_sign), .in1(adder_and_subtracter_1_sign), .in2(dividor_1_q4),
    .in3(multiplication_1_z8), .out(Sign), .sel({S2, S1}));
  not not_1 (Zero_flag, or_1_out);
  Binary_To_BCD binary_to_bcd_1 (
    .B0(multiplexer_9_out[0]), .B1(multiplexer_9_out[1]), .B2(multiplexer_9_out[2]),
    .B3(multiplexer_9_out[3]), .B4(multiplexer_9_out[4]), .B5(multiplexer_9_out[5]),
    .B6(multiplexer_9_out[6]), .B7(multiplexer_9_out[7]), .out_9(binary_to_bcd_1_out_9),
    .out_10(binary_to_bcd_1_out_10), .out_11(binary_to_bcd_1_out_11), .out_12(binary_to_bcd_1_out_12),
    .out_13(binary_to_bcd_1_out_13), .out_14(binary_to_bcd_1_out_14), .out_15(binary_to_bcd_1_out_15),
    .out_16(binary_to_bcd_1_out_16), .out_17(binary_to_bcd_1_out_17), .out_18(binary_to_bcd_1_out_18),
    .out_19(binary_to_bcd_1_out_19), .out_20(binary_to_bcd_1_out_20));
  Multiplexer #(.select(2), .enable("false")) multiplexer_2 (
    .in0(1'b0), .in1(1'b0), .in2(1'b0), .in3(multiplication_1_z7), .out(multiplexer_9_out[7]), .sel({S2, S1}));
  BCD_TO_7_SEGMENT _7_Segment_1 (
    .X0(binary_to_bcd_1_out_9), .X1(binary_to_bcd_1_out_10), .X2(binary_to_bcd_1_out_11),
    .X3(binary_to_bcd_1_out_12), .out_5(_7_Segment_1_a), .out_6(_7_Segment__1_b), .out_7(_7_Segment_1_c),
    .out_8(_7_Segment_1_d), .out_9(_7_Segment_1_e), .out_10(_7_Segment_1_f), .out_11(_7_Segment_1_g));
  BCD_TO_7_SEGMENT _7_Segment_2 (
    .X0(binary_to_bcd_1_out_13), .X1(binary_to_bcd_1_out_14), .X2(binary_to_bcd_1_out_15),
    .X3(binary_to_bcd_1_out_16), .out_5(_7_Segment_2_a), .out_6(_7_Segment_2_b), .out_7(_7_Segment_2_c),
    .out_8(_7_Segment_2_d), .out_9(_7_Segment_2_e), .out_10(_7_Segment_2_f), .out_11(_7_Segment_2_g));
  BCD_TO_7_SEGMENT _7_Segment_3 (
    .X0(binary_to_bcd_1_out_17), .X1(binary_to_bcd_1_out_18), .X2(binary_to_bcd_1_out_19),
    .X3(binary_to_bcd_1_out_20), .out_5(_7_Segment_3_a), .out_6(_7_Segment_3_b), .out_7(_7_Segment_3_c),
    .out_8(_7_Segment_3_d), .out_9(_7_Segment_3_e), .out_10(_7_Segment_3_f), .out_11(_7_Segment_3_g));
  Multiplexer #(.select(2), .enable("false")) multiplexer_3 (
    .in0(1'b0), .in1(1'b0), .in2(1'b0), .in3(multiplication_1_z6), .out(multiplexer_9_out[6]), .sel({S2, S1}));
  or or_1 (or_1_out, multiplexer_9_out[7], or_2_out);
  or or_2 (or_2_out, multiplexer_9_out[6], or_3_out);
  Multiplication multiplication_1 (
    .A0(A[0]), .A1(A[1]), .A2(A[2]), .A3(A[3]), .A4(A[4]), .B0(B[0]), .B1(B[1]), .B2(B[2]), .B3(B[3]),
    .B4(B[4]), .Z0(multiplication_1_z0), .Z1(multiplication_1_z1), .Z2(multiplication_1_z2),
    .Z3(multiplication_1_z3), .Z4(multiplication_1_z4), .Z5(multiplication_1_z5), .Z6(multiplication_1_z6),
    .Z7(multiplication_1_z7), .Z8(multiplication_1_z8));
  Multiplexer #(.select(2), .enable("false")) multiplexer_4 (
    .in0(1'b0), .in1(1'b0), .in2(1'b0), .in3(multiplication_1_z5), .out(multiplexer_9_out[5]), .sel({S2, S1}));
  or or_3 (or_3_out, or_4_out, multiplexer_9_out[5]);
  Dividor dividor_1 (
    .A0(A[0]), .A1(A[1]), .A2(A[2]), .A3(A[3]), .A4(A[4]), .B0(B[0]), .B1(B[1]), .B2(B[2]), .B3(B[3]),
    .B4(B[4]), .Q0(dividor_1_q0), .Q1(dividor_1_q1), .Q2(dividor_1_q2), .Q3(dividor_1_q3), .Q4(dividor_1_q4),
    .Dev_0_Flag(Division_by_0));
  Multiplexer #(.select(2), .enable("false")) multiplexer_5 (
    .in0(adder_and_subtracter_1_cout), .in1(adder_and_subtracter_1_cout), .in2(1'b0),
    .in3(multiplication_1_z4), .out(multiplexer_9_out[4]), .sel({S2, S1}));
  or or_4 (or_4_out, multiplexer_9_out[4], or_5_out);
  or or_5 (or_5_out, multiplexer_9_out[3], or_6_out);
  or or_6 (or_6_out, multiplexer_9_out[2], or_7_out);
  Multiplexer #(.select(2), .enable("false")) multiplexer_6 (
    .in0(adder_and_subtracter_1_out_3), .in1(adder_and_subtracter_1_out_3), .in2(dividor_1_q3),
    .in3(multiplication_1_z3), .out(multiplexer_9_out[3]), .sel({S2, S1}));
  Multiplexer #(.select(2), .enable("false")) multiplexer_7 (
    .in0(adder_and_subtracter_1_out_2), .in1(adder_and_subtracter_1_out_2), .in2(dividor_1_q2),
    .in3(multiplication_1_z2), .out(multiplexer_9_out[2]), .sel({S2, S1}));
  or or_7 (or_7_out, multiplexer_9_out[1], multiplexer_9_out[0]);
  Multiplexer #(.select(2), .enable("false")) multiplexer_8 (
    .in0(adder_and_subtracter_1_out_1), .in1(adder_and_subtracter_1_out_1), .in2(dividor_1_q1),
    .in3(multiplication_1_z1), .out(multiplexer_9_out[1]), .sel({S2, S1}));
  Adder_and_subtracter adder_and_subtracter_1 (
    .B(B[3:0]), .A(A[3:0]), .Sign(adder_and_subtracter_1_sign), .Cout(adder_and_subtracter_1_cout),
    .Out_3(adder_and_subtracter_1_out_3), .Out_2(adder_and_subtracter_1_out_2),
    .Out_1(adder_and_subtracter_1_out_1), .Out_0(adder_and_subtracter_1_out_0), .A_sign(A[4]), .B_sign(B[4]),
    .Cin(S1));
  Multiplexer #(.select(2), .enable("false")) multiplexer_9 (
    .in0(adder_and_subtracter_1_out_0), .in1(adder_and_subtracter_1_out_0), .in2(dividor_1_q0),
    .in3(multiplication_1_z0), .out(multiplexer_9_out[0]), .sel({S2, S1}));
endmodule
