// Logisim project Multiplication.circ as structural Verilog
module Half_Adder (
  input  A,
  input  B,
  output Sun,
  output Carry
);

  xor xor_1 (Sun, A, B);
  and and_1 (Carry, A, B);
endmodule

module Full_Adder (
  input  A,
  input  B,
  input  C,
  output Sum,
  output Carry
);

  wire and_1_out, and_2_out, xor_1_out;

  xor xor_1 (xor_1_out, A, B);
  and and_1 (and_1_out, xor_1_out, C);
  and and_2 (and_2_out, A, B);
  xor xor_2 (Sum, xor_1_out, C);
  or or_1 (Carry, and_1_out, and_2_out);
endmodule

module Multiplication (
  input  A0,
  input  A1,
  input  A2,
  input  A3,
  input  A4,
  input  B0,
  input  B1,
  input  B2,
  input  B3,
  input  B4,
  output Z0,
  output Z1,
  output Z2,
  output Z3,
  output Z4,
  output Z5,
  output Z6,
  output Z7,
  output Z8
);

  wire and_2_out, and_3_out, and_4_out, and_5_out, and_6_out, and_7_out, and_8_out, and_9_out, and_10_out,
       and_11_out, and_12_out, and_13_out, and_14_out, and_15_out, and_16_out, full_adder_1_carry,
       full_adder_1_sum, full_adder_2_carry, full_adder_2_sum, full_adder_3_carry, full_adder_3_sum,
       full_adder_4_carry, full_adder_4_sum, full_adder_5_carry, full_adder_6_carry, full_adder_6_sum,
       full_adder_8_carry, half_adder_1_carry, half_adder_2_carry, half_adder_3_carry, half_adder_4_carry,
       half_adder_4_sun;

  and and_1 (Z0, A0, B0);
  and and_2 (and_2_out, A1, B0);
  and and_3 (and_3_out, A2, B0);
  and and_4 (and_4_out, A3, B0);
  and and_5 (and_5_out, A0, B1);
  and and_6 (and_6_out, A1, B1);
  and and_7 (and_7_out, A2, B1);
  and and_8 (and_8_out, A3, B1);
  and and_9 (and_9_out, A0, B2);
  and and_10 (and_10_out, A1, B2);
  and and_11 (and_11_out, A2, B2);
  and and_12 (and_12_out, A3, B2);
  and and_13 (and_13_out, A0, B3);
  and and_14 (and_14_out, A1, B3);
  and and_15 (and_15_out, A2, B3);
  and and_16 (and_16_out, A3, B3);
  Half_Adder half_adder_1 (.A(and_2_out), .B(and_5_out), .Sun(Z1), .Carry(half_adder_1_carry));
  Full_Adder full_adder_1 (
    .A(half_adder_1_carry), .B(and_3_out), .C(and_6_out), .Sum(full_adder_1_sum), .Carry(full_adder_1_carry));
  Full_Adder full_adder_2 (
    .A(full_adder_1_carry), .B(and_4_out), .C(and_7_out), .Sum(full_adder_2_sum), .Carry(full_adder_2_carry));
  Full_Adder full_adder_3 (
    .A(full_adder_6_carry), .B(and_12_out), .C(half_adder_4_carry), .Sum(full_adder_3_sum),
    .Carry(full_adder_3_carry));
  Half_Adder half_adder_2 (.A(full_adder_1_sum), .B(and_9_out), .Sun(Z2), .Carry(half_adder_2_carry));
  Full_Adder full_adder_4 (
    .A(half_adder_2_carry), .B(full_adder_2_sum), .C(and_10_out), .Sum(full_adder_4_sum),
    .Carry(full_adder_4_carry));
  Half_Adder half_adder_3 (.A(full_adder_4_sum), .B(and_13_out), .Sun(Z3), .Carry(half_adder_3_carry));
  Half_Adder half_adder_4 (.A(full_adder_2_carry), .B(and_8_out), .Sun(half_adder_4_sun), .Carry(half_adder_4_carry));
  Full_Adder full_adder_5 (
    .A(full_adder_8_carry), .B(and_15_out), .C(full_adder_3_sum), .Sum(Z5), .Carry(full_adder_5_carry));
  Full_Adder full_adder_6 (
    .A(full_adder_4_carry), .B(half_adder_4_sun), .C(and_11_out), .Sum(full_adder_6_sum),
    .Carry(full_adder_6_carry));
  Full_Adder full_adder_7 (.A(full_adder_5_carry), .B(and_16_out), .C(full_adder_3_carry), .Sum(Z6), .Carry(Z7));
  xor xor_1 (Z8, A4, B4);
  Full_Adder full_adder_8 (
    .A(half_adder_3_carry), .B(full_adder_6_sum), .C(and_14_out), .Sum(Z4), .Carry(full_adder_8_carry));

  // Notes on the sheet:
  //   10
  //   7
  //   11
  //   8
  //   9
endmodule
