// Logisim project bcd to 7 seg2.circ as structural Verilog: 9 circuits, main circuit main
module main (
  input  in_1,
  input  in_2,
  input  X2,
  input  in_4,
  input  X3
);

  wire bcd_to_7_segment_1_out_5, bcd_to_7_segment_1_out_6, bcd_to_7_segment_1_out_7,
       bcd_to_7_segment_1_out_8, bcd_to_7_segment_1_out_9, bcd_to_7_segment_1_out_10,
       bcd_to_7_segment_1_out_11;

  BCD_TO_7_SEGMENT bcd_to_7_segment_1 (
    .X0(in_1), .X1(in_2), .X2(X2), .X3(X3), .out_5(bcd_to_7_segment_1_out_5),
    .out_6(bcd_to_7_segment_1_out_6), .out_7(bcd_to_7_segment_1_out_7), .out_8(bcd_to_7_segment_1_out_8),
    .out_9(bcd_to_7_segment_1_out_9), .out_10(bcd_to_7_segment_1_out_10), .out_11(bcd_to_7_segment_1_out_11));
  _7_Segment_Display u_7_segment_display_1 (
    .g(bcd_to_7_segment_1_out_11), .f(bcd_to_7_segment_1_out_10), .a(bcd_to_7_segment_1_out_5),
    .b(bcd_to_7_segment_1_out_6), .e(bcd_to_7_segment_1_out_9), .d(bcd_to_7_segment_1_out_8),
    .c(bcd_to_7_segment_1_out_7), .dp(in_4));

  // Notes on the sheet:
  //   X0
  //   X1
endmodule

module BCD_TO_7_SEGMENT (
  input  X0,
  input  X1,
  input  X2,
  input  X3,
  output out_5,
  output out_6,
  output out_7,
  output out_8,
  output out_9,
  output out_10,
  output out_11
);

  A a_1 (.in_1(X0), .in_2(X1), .X2(X2), .X3(X3), .out_5(out_5));
  B b_1 (.X0(X0), .X1(X1), .X2(X2), .X3(X3), .out_5(out_6));
  C c_1 (.X0(X0), .X1(X1), .in_3(X2), .in_4(X3), .out_5(out_7));
  D d_1 (.in_1(X0), .in_2(X1), .X2(X2), .in_4(X3), .out_5(out_8));
  E e_1 (.X0(X0), .X1(X1), .X2(X2), .X3(X3), .out_5(out_9));
  F f_1 (.X0(X0), .X1(X1), .X2(X2), .in_4(X3), .out_5(out_10));
  G g_1 (.X0(X0), .X1(X1), .X2(X2), .X3(X3), .out_5(out_11));

  // Notes on the sheet:
  //   A
  //   B
  //   C
  //   D
  //   E
  //   F
  //   G
endmodule

module A (
  input  in_1,
  input  in_2,
  input  X2,
  input  X3,
  output out_5
);

  wire or_1_out, xnor_1_out;

  xnor xnor_1 (xnor_1_out, in_1, X2);
  or or_1 (or_1_out, xnor_1_out, in_2);
  or or_2 (out_5, or_1_out, X3);

  // Notes on the sheet:
  //   X0
  //   X1
endmodule

module B (
  input  X0,
  input  X1,
  input  X2,
  input  X3,
  output out_5
);

  wire not_1_out, or_1_out, xnor_1_out;

  not not_1 (not_1_out, X2);
  xnor xnor_1 (xnor_1_out, X0, X1);
  or or_1 (or_1_out, xnor_1_out, not_1_out);
  or or_2 (out_5, or_1_out, X3);
endmodule

module C (
  input  X0,
  input  X1,
  input  in_3,
  input  in_4,
  output out_5
);

  wire not_1_out, or_1_out;

  not not_1 (not_1_out, X1);
  or or_1 (or_1_out, X0, not_1_out);
  or or_2 (out_5, or_1_out, in_3);

  // Notes on the sheet:
  //   X2
  //   X3
endmodule

module D (
  input  in_1,
  input  in_2,
  input  X2,
  input  in_4,
  output out_5
);

  wire and_1_out, and_2_out, and_3_out, and_4_out, not_1_out, not_2_out, not_3_out, or_1_out, or_2_out,
       or_3_out;

  not not_1 (not_1_out, in_1);
  not not_2 (not_2_out, X2);
  not not_3 (not_3_out, in_2);
  and and_1 (and_1_out, not_1_out, in_2);
  and and_2 (and_2_out, in_2, not_2_out);
  and and_3 (and_3_out, not_1_out, not_2_out);
  and and_4 (and_4_out, in_1, X2, not_3_out);
  or or_1 (or_1_out, and_1_out, and_2_out);
  or or_2 (or_2_out, or_1_out, and_3_out);
  or or_3 (or_3_out, or_2_out, and_4_out);
  or or_4 (out_5, or_3_out, in_4);

  // Notes on the sheet:
  //   X0
  //   X1
  //   X3
endmodule

module E (
  input  X0,
  input  X1,
  input  X2,
  input  X3,
  output out_5
);

  wire and_1_out, and_2_out, not_1_out, not_2_out;

  not not_1 (not_1_out, X0);
  not not_2 (not_2_out, X2);
  and and_1 (and_1_out, not_1_out, X1);
  and and_2 (and_2_out, not_1_out, not_2_out);
  or or_1 (out_5, and_1_out, and_2_out);
endmodule

module F (
  input  X0,
  input  X1,
  input  X2,
  input  in_4,
  output out_5
);

  wire and_1_out, and_2_out, and_3_out, not_1_out, not_2_out, or_1_out, or_2_out;

  not not_1 (not_1_out, X1);
  not not_2 (not_2_out, X0);
  and and_1 (and_1_out, not_2_out, not_1_out);
  and and_2 (and_2_out, X2, not_2_out);
  and and_3 (and_3_out, not_1_out, X2);
  or or_1 (or_1_out, and_2_out, and_1_out);
  or or_2 (or_2_out, or_1_out, and_3_out);
  or or_3 (out_5, or_2_out, in_4);

  // Notes on the sheet:
  //   X3
endmodule

module G (
  input  X0,
  input  X1,
  input  X2,
  input  X3,
  output out_5
);

  wire and_1_out, not_1_out, or_1_out, xor_1_out;

  not not_1 (not_1_out, X0);
  and and_1 (and_1_out, not_1_out, X1);
  xor xor_1 (xor_1_out, X1, X2);
  or or_1 (or_1_out, and_1_out, xor_1_out);
  or or_2 (out_5, or_1_out, X3);
endmodule
